// Logisim project TallerLogica-Combinatorios.circ as structural Verilog: 12 circuits, main circuit verificador
module sumador_simple (
  input  A,
  input  B,
  output S,
  output Cout
);

  xor xor_1 (S, A, B);
  and and_1 (Cout, A, B);
endmodule

module sumador_completo (
  input  Cin,
  input  A,
  input  B,
  output S,
  output Cout
);

  wire sumador_simple_1_cout, sumador_simple_1_s, sumador_simple_2_cout;

  sumador_simple sumador_simple_1 (.A(A), .B(B), .S(sumador_simple_1_s), .Cout(sumador_simple_1_cout));
  sumador_simple sumador_simple_2 (.A(Cin), .B(sumador_simple_1_s), .S(S), .Cout(sumador_simple_2_cout));
  or or_1 (Cout, sumador_simple_2_cout, sumador_simple_1_cout);
endmodule

module sumador_4 (
  input  Cin,
  input  [3:0] A,
  input  [3:0] B,
  output [3:0] S,
  output Cout
);

  wire sumador_completo_1_cout, sumador_completo_2_cout, sumador_completo_3_cout;

  sumador_completo sumador_completo_1 (.Cin(Cin), .A(A[0]), .B(B[0]), .S(S[0]), .Cout(sumador_completo_1_cout));
  sumador_completo sumador_completo_2 (
    .Cin(sumador_completo_1_cout), .A(A[1]), .B(B[1]), .S(S[1]), .Cout(sumador_completo_2_cout));
  sumador_completo sumador_completo_3 (
    .Cin(sumador_completo_2_cout), .A(A[2]), .B(B[2]), .S(S[2]), .Cout(sumador_completo_3_cout));
  sumador_completo sumador_completo_4 (.Cin(sumador_completo_3_cout), .A(A[3]), .B(B[3]), .S(S[3]), .Cout(Cout));
  Hex_Digit_Display hex_digit_display_1 (.value(S));  // open: dp
endmodule

module comparador_cero (
  input  [3:0] A,
  output Z
);

  wire and_1_out, and_2_out, not_1_out, not_2_out, not_3_out, not_4_out;

  not not_1 (not_1_out, A[0]);
  not not_2 (not_2_out, A[1]);
  not not_3 (not_3_out, A[2]);
  not not_4 (not_4_out, A[3]);
  and and_1 (and_1_out, not_1_out, not_2_out);
  and and_2 (and_2_out, not_3_out, not_4_out);
  and and_3 (Z, and_1_out, and_2_out);
endmodule

module sumador_flags (
  input  Cin,
  input  [3:0] A,
  input  [3:0] B,
  output [3:0] S,
  output N,
  output Z,
  output V,
  output C
);

  wire not_1_out, xor_1_out, xor_2_out;

  xor xor_1 (xor_1_out, B[3], A[3]);
  not not_1 (not_1_out, xor_1_out);
  sumador_4 sumador_4_1 (.Cin(Cin), .A(A), .B(B), .S({N, S[2:0]}), .Cout(C));
  Hex_Digit_Display hex_digit_display_1 (.value({N, S[2:0]}));  // open: dp
  xor xor_2 (xor_2_out, A[3], N);
  and and_1 (V, xor_2_out, not_1_out);
  comparador_cero comparador_cero_1 (.A({N, S[2:0]}), .Z(Z));

  assign S[3] = N;
endmodule

module incrementador_4 (
  input  [3:0] A,
  output [3:0] S
);

  sumador_4 sumador_4_1 (.Cin(1'b1), .A(A), .B(4'b0000), .S(S));  // open: Cout
  Hex_Digit_Display hex_digit_display_1 (.value(S));  // open: dp
endmodule

module inversor_4 (
  input  [3:0] A,
  input  INV,
  output [3:0] S
);

  wire [3:0] incrementador_4_1_s, not_1_out;

  assign not_1_out = ~A;  // NOT_Gate not_1, 4 bits wide
  incrementador_4 incrementador_4_1 (.A(not_1_out), .S(incrementador_4_1_s));
  Multiplexer #(.width(4)) multiplexer_1 (.in0(A), .in1(incrementador_4_1_s), .out(S), .sel(INV));
  Hex_Digit_Display hex_digit_display_1 (.value(S));  // open: dp
endmodule

module ALU (
  input  [3:0] A,
  input  [3:0] B,
  input  [1:0] OP,
  output N,
  output Z,
  output V,
  output C,
  output [3:0] S
);

  wire sumaresta_1_c, sumaresta_1_v;
  wire [3:0] and4b_1_s, or4b_1_s, sumaresta_1_s;

  sumaresta sumaresta_1 (
    .A(A), .B(B), .in_3(OP[0]), .S(sumaresta_1_s), .V(sumaresta_1_v), .C(sumaresta_1_c));  // open: N, Z
  and4b and4b_1 (.A(A), .B(B), .s(and4b_1_s));  // open: N, Z
  or4b or4b_1 (.A(A), .B(B), .s(or4b_1_s));  // open: N, Z
  Multiplexer #(.select(2), .width(4)) multiplexer_1 (
    .in0(sumaresta_1_s), .in1(sumaresta_1_s), .in2(and4b_1_s), .in3(or4b_1_s), .out({N, S[2:0]}), .sel(OP));
  Multiplexer #(.select(2)) multiplexer_2 (
    .in0(sumaresta_1_v), .in1(sumaresta_1_v), .in2(1'b0), .in3(1'b0), .out(V), .sel(OP));
  Multiplexer #(.select(2)) multiplexer_3 (
    .in0(sumaresta_1_c), .in1(sumaresta_1_c), .in2(1'b0), .in3(1'b0), .out(C), .sel(OP));
  Hex_Digit_Display hex_digit_display_1 (.value({N, S[2:0]}));  // open: dp
  comparador_cero comparador_cero_1 (.A({N, S[2:0]}), .Z(Z));

  assign S[3] = N;
endmodule

module verificador (
  output [3:0] out_1,
  output [3:0] out_2,
  output [1:0] out_3,
  output halt,
  output N,
  output Z,
  output V,
  output C,
  output [3:0] res
);

  wire clock_1_out;

  Clock clock_1 (.out(clock_1_out));
  Counter #(.max('h3ff), .width(10)) counter_1 (
    .clk(clock_1_out), .carry(halt), .Q({out_3, out_2, out_1}));  // open: clr, load, up, count, D
  ALU alu_1 (.A(out_1), .B(out_2), .OP(out_3), .N(N), .Z(Z), .V(V), .C(C), .S(res));
endmodule

module and4b (
  input  [3:0] A,
  input  [3:0] B,
  output [3:0] s,
  output N,
  output Z
);

  and and_1 (s[0], A[0], B[0]);
  and and_2 (s[1], A[1], B[1]);
  and and_3 (s[2], A[2], B[2]);
  and and_4 (N, A[3], B[3]);
  comparador_cero comparador_cero_1 (.A({N, s[2:0]}), .Z(Z));

  assign s[3] = N;
endmodule

module or4b (
  input  [3:0] A,
  input  [3:0] B,
  output [3:0] s,
  output N,
  output Z
);

  or or_1 (s[0], A[0], B[0]);
  or or_2 (s[1], A[1], B[1]);
  or or_3 (s[2], A[2], B[2]);
  or or_4 (N, A[3], B[3]);
  comparador_cero comparador_cero_1 (.A({N, s[2:0]}), .Z(Z));

  assign s[3] = N;
endmodule

module sumaresta (
  input  [3:0] A,
  input  [3:0] B,
  input  in_3,
  output [3:0] S,
  output N,
  output Z,
  output V,
  output C
);

  wire and_1_out, and_2_out, and_3_out, and_4_out, comparador_cero_1_z, multiplexer_1_out, not_1_out,
       not_2_out, not_3_out, not_4_out, not_5_out, sumador_flags_1_c, sumador_flags_1_v;
  wire [3:0] inversor_4_1_s;

  not not_1 (not_1_out, B[0]);
  not not_2 (not_2_out, B[1]);
  not not_3 (not_3_out, B[2]);
  inversor_4 inversor_4_1 (.A(B), .INV(in_3), .S(inversor_4_1_s));
  comparador_cero comparador_cero_1 (.A(B), .Z(comparador_cero_1_z));
  and and_1 (and_1_out, not_1_out, not_2_out);
  and and_2 (and_2_out, not_3_out, B[3]);
  not not_4 (not_4_out, comparador_cero_1_z);
  and and_3 (and_3_out, and_1_out, and_2_out);
  sumador_flags sumador_flags_1 (
    .Cin(1'b0), .A(A), .B(inversor_4_1_s), .S(S), .N(N), .Z(Z), .V(sumador_flags_1_v), .C(sumador_flags_1_c));
  not not_5 (not_5_out, sumador_flags_1_c);
  and and_4 (and_4_out, and_3_out, in_3);
  Multiplexer multiplexer_1 (.in0(sumador_flags_1_c), .in1(not_5_out), .out(multiplexer_1_out), .sel(in_3));
  and and_5 (C, multiplexer_1_out, not_4_out);
  or or_1 (V, sumador_flags_1_v, and_4_out);
endmodule
