// Logisim project guia_2.circ as structural Verilog: 15 circuits, main circuit main
module main (
  input  clk,
  input  [3:0] bus_in,
  input  read,
  input  load,
  input  inc,
  output [3:0] out_6
);

  wire not_1_out;
  wire [3:0] controlled_buffer_1_out, sumbin4b_1_s;

  bidirReg4b bidirreg4b_1 (.clk(clk), .read(read), .load(load), .bus_out(out_6), .bus_in(controlled_buffer_1_out));
  sumBin4b sumbin4b_1 (.a(4'b0001), .b(out_6), .s(sumbin4b_1_s));  // open: cO
  assign controlled_buffer_1_out = inc ? sumbin4b_1_s : 4'bz;  // Controlled_Buffer controlled_buffer_1
  assign controlled_buffer_1_out = not_1_out ? bus_in : 4'bz;  // Controlled_Buffer controlled_buffer_2
  not not_1 (not_1_out, inc);

  // Notes on the sheet:
  //   out_6: pull=up
  //   bus_in: pull=up
endmodule

module demultiplexor (
  input  c1,
  input  c0,
  input  e0,
  output s0,
  output s1,
  output s2,
  output s3
);

  and and_1 (s0, ~c1, e0, ~c0);  // AND_Gate
  and and_2 (s1, ~c1, e0, c0);  // AND_Gate
  and and_3 (s2, c1, e0, ~c0);  // AND_Gate
  and and_4 (s3, c1, e0, c0);
endmodule

module inversor (
  input  e2,
  input  e1,
  input  e0,
  input  c0,
  output s2,
  output s1,
  output s0
);

  xor xor_1 (s2, c0, e2);
  xor xor_2 (s1, c0, e1);
  xor xor_3 (s0, c0, e0);
endmodule

module inversoAditivo (
  input  [3:0] e,
  output [3:0] s,
  output nr
);

  wire [3:0] not_1_out;

  assign not_1_out = ~e;  // NOT_Gate not_1, 4 bits wide
  and and_1 (nr, ~e[0], ~e[1], ~e[2], e[3]);  // AND_Gate
  sumBin4b sumbin4b_1 (.a(not_1_out), .b(4'b0001), .s(s));  // open: cO
endmodule

module sumBin4b (
  input  [3:0] a,
  input  [3:0] b,
  output cO,
  output [3:0] s
);

  wire sumbin1b_2_co, sumbin1b_3_co, sumbin1b_4_co;

  sumBin1b sumbin1b_1 (.cO(cO), .e1(b[3]), .e0(a[3]), .res(s[3]), .cI(sumbin1b_2_co));
  sumBin1b sumbin1b_2 (.cO(sumbin1b_2_co), .e1(b[2]), .e0(a[2]), .res(s[2]), .cI(sumbin1b_3_co));
  sumBin1b sumbin1b_3 (.cO(sumbin1b_3_co), .e1(b[1]), .e0(a[1]), .res(s[1]), .cI(sumbin1b_4_co));
  sumBin1b sumbin1b_4 (.cO(sumbin1b_4_co), .e1(b[0]), .e0(a[0]), .res(s[0]), .cI(1'b0));
endmodule

module sumBin1b (
  input  e1,
  input  e0,
  input  cI,
  output cO,
  output res
);

  wire and_1_out, and_2_out, xor_1_out;

  or or_1 (cO, and_1_out, and_2_out);
  and and_1 (and_1_out, e0, e1);
  and and_2 (and_2_out, cI, xor_1_out);
  xor xor_1 (xor_1_out, e1, e0);
  xor xor_2 (res, xor_1_out, cI);
endmodule

module codificador (
  input  [3:0] e,
  output [1:0] s,
  output v
);

  or or_1 (s[0], e[1], e[3]);
  or or_2 (s[1], e[2], e[3]);
  ExactlyOne xor_1 (.out(v), .in0(e[0]), .in1(e[1]), .in2(e[2]), .in3(e[3]));
endmodule

module decodificador (
  input  [1:0] e,
  output [3:0] s
);

  and and_1 (s[0], ~e[0], ~e[1]);  // AND_Gate
  and and_2 (s[1], e[0], ~e[1]);  // AND_Gate
  and and_3 (s[2], ~e[0], e[1]);  // AND_Gate
  and and_4 (s[3], e[0], e[1]);
endmodule

module demultiplex (
  input  e,
  input  c0,
  input  c1,
  output s0,
  output s1,
  output s2,
  output s3
);

  wire [3:0] decodificador_1_s;

  decodificador decodificador_1 (.e({c1, c0}), .s(decodificador_1_s));
  and and_1 (s0, e, decodificador_1_s[0]);
  and and_2 (s1, e, decodificador_1_s[1]);
  and and_3 (s2, e, decodificador_1_s[2]);
  and and_4 (s3, e, decodificador_1_s[3]);
endmodule

module sReg4b (
  input  [3:0] i,
  input  load,
  input  clk,
  output [3:0] o
);

  wire and_1_out;

  and and_1 (and_1_out, load, clk);
  D_Flip_Flop d_ff_1 (.D(i[0]), .clk(and_1_out), .Q(o[0]));  // open: Qn, preset, reset
  D_Flip_Flop d_ff_2 (.D(i[1]), .clk(and_1_out), .Q(o[1]));  // open: Qn, preset, reset
  D_Flip_Flop d_ff_3 (.D(i[2]), .clk(and_1_out), .Q(o[2]));  // open: Qn, preset, reset
  D_Flip_Flop d_ff_4 (.D(i[3]), .clk(and_1_out), .Q(o[3]));  // open: Qn, preset, reset
endmodule

module bidirReg4b (
  input  [3:0] bus_in,
  input  clk,
  input  read,
  input  load,
  output [3:0] bus_out
);

  wire and_1_out, not_1_out, xor_1_out;
  wire [3:0] sreg4b_1_o;

  sReg4b sreg4b_1 (.load(load), .clk(and_1_out), .i(bus_out), .o(sreg4b_1_o));
  and and_1 (and_1_out, clk, xor_1_out);
  xor xor_1 (xor_1_out, load, read);
  assign bus_out = read ? sreg4b_1_o : 4'bz;  // Controlled_Buffer controlled_buffer_1
  assign bus_out = not_1_out ? bus_in : 4'bz;  // Controlled_Buffer controlled_buffer_2
  not not_1 (not_1_out, read);

  // Notes on the sheet:
  //   bus_out: pull=up
  //   bus_in: pull=up
endmodule

module signExtenderReg4b (
  input  [3:0] i,
  input  clk,
  input  load,
  input  ext,
  output [3:0] o
);

  wire not_1_out;
  wire [3:0] sreg4b_1_o;

  sReg4b sreg4b_1 (.load(load), .clk(clk), .i(i), .o(sreg4b_1_o));
  Multiplexer #(.width(4)) multiplexer_1 (
    .in0({{3{sreg4b_1_o[1]}}, sreg4b_1_o[0]}), .in1(sreg4b_1_o), .out(o), .sel(not_1_out));
  not not_1 (not_1_out, ext);
endmodule

module LdisplacerReg4b (
  input  [3:0] i,
  input  clk,
  input  load,
  input  shl,
  output [3:0] o
);

  wire not_1_out;
  wire [3:0] shiftlr4b_1_o, sreg4b_1_o;

  sReg4b sreg4b_1 (.load(load), .clk(clk), .i(i), .o(sreg4b_1_o));
  shiftLR4b shiftlr4b_1 (.i(sreg4b_1_o), .left(1'b1), .o(shiftlr4b_1_o));
  Multiplexer #(.width(4)) multiplexer_1 (.in0(shiftlr4b_1_o), .in1(sreg4b_1_o), .out(o), .sel(not_1_out));
  not not_1 (not_1_out, shl);
endmodule

module shiftLR4b (
  input  [3:0] i,
  input  left,
  output [3:0] o
);

  wire and_1_out, and_3_out, and_4_out, and_6_out, not_1_out;

  not not_1 (not_1_out, left);
  and and_1 (and_1_out, not_1_out, i[3]);
  and and_2 (o[3], left, i[2]);
  and and_3 (and_3_out, not_1_out, i[2]);
  and and_4 (and_4_out, left, i[1]);
  and and_5 (o[0], not_1_out, i[1]);
  and and_6 (and_6_out, left, i[0]);
  or or_1 (o[1], and_6_out, and_3_out);
  or or_2 (o[2], and_4_out, and_1_out);
endmodule

module selfIncReg4b (
  input  [3:0] bus_in,
  input  read,
  input  load,
  input  inc,
  input  clk,
  output [3:0] bus_out
);

  wire and_1_out, nor_1_out, not_1_out, not_2_out, or_1_out, xor_1_out;
  wire [3:0] bsi, controlled_buffer_1_out, sreg4b_1_o, sumbin4b_1_s;

  or or_1 (or_1_out, load, inc);
  not not_1 (not_1_out, clk);
  ExactlyOne xor_1 (.out(xor_1_out), .in0(inc), .in1(load), .in2(read));
  sumBin4b sumbin4b_1 (.a(sreg4b_1_o), .b(4'b0001), .s(sumbin4b_1_s));  // open: cO
  assign controlled_buffer_1_out = inc ? sumbin4b_1_s : 4'bz;  // Controlled_Buffer controlled_buffer_1
  assign controlled_buffer_1_out = not_2_out ? sreg4b_1_o : 4'bz;  // Controlled_Buffer controlled_buffer_2
  and and_1 (and_1_out, or_1_out, xor_1_out, not_1_out);
  sReg4b sreg4b_1 (.load(and_1_out), .clk(clk), .o(sreg4b_1_o));  // open: i
  not not_2 (not_2_out, inc);
  assign bus_out = read ? sreg4b_1_o : 4'bz;  // Controlled_Buffer controlled_buffer_3
  assign bsi = nor_1_out ? bus_in : 4'bz;  // Controlled_Buffer controlled_buffer_4
  nor nor_1 (nor_1_out, read, inc);

  // Notes on the sheet:
  //   bus_out: pull=up
  //   bus_in: pull=up
endmodule
