// Logisim project latch_jk.circ as structural Verilog: 1 circuit, main circuit main
module main (
);

  wire and_1_out, and_2_out, dipswitch_1_p1, dipswitch_1_p2, nor_1_out, nor_2_out;

  // DipSwitch #(.number(2)) dipswitch_1: pin names not known; wires that end beside it: dipswitch_1_p1, dipswitch_1_p2
  and and_1 (and_1_out, nor_2_out, dipswitch_1_p2);
  and and_2 (and_2_out, nor_1_out, dipswitch_1_p1);
  nor nor_1 (nor_1_out, and_2_out, nor_2_out);
  nor nor_2 (nor_2_out, nor_1_out, and_1_out);
  LedBar #(.matrixcols(2)) ledbar_1 (.led0(nor_1_out), .led1(nor_2_out));
endmodule
